# Fritzing sketch temperature_sensor (saved by Fritzing 0.8.7b)
breadboards: 1

parts:
  R1 = PHOTOCELL [package=photocell-kit]
  R2 = Resistor [tolerance=±5% resistance=220 package=THT]
  C1 = Capacitor [package=cap-pth-small2]
  C9 = Capacitor Polarized [package=nippon_f80]
  U2 = TMP36 [package=to-92-kit]
  U3 = V_REG_LD1117VXX [package=78xxl]
  LED2 = LEDs [package=led10mm]
  U5 = XBEE-1 [package=xbee-1_lock]
  U4 = TMP36 [package=to-92-kit]
  S2 = Momentary Switch [package=ksa_sealed_tac_switch]
  LED3 = RGB LED (com. anode, rbg) [package="5 mm [THT]"]
  R3 = Resistor [tolerance=±5% resistance=220 package=THT]
  X1 = USB Connectors [package=usb-minib]

nets:
  N1: R1.P$1, R2.Pin_0, U5.DIO1
  GND: R1.P$2, C1.1, C9.-, U2.GND, U3.GND, LED2.A, U5.GND, U4.GND, S2.1, X1.GND
  VCC: R2.Pin_1, C9.+, U2.VCC, U3.OUT, U5.VDD, U4.VCC
  N2: C1.2, U3.IN, X1.VBUS
  N3: U2.VOUT, U5.DIO0
  N4: LED2.C, U5.DIO11
  N5: U5.DIO9, LED3.green_cathode
  N6: U5.DIO5, LED3.blue_cathode
  N7: U5.DIO3, LED3.red_cathode
  N8: U5.DIO2, U4.VOUT
  N9: S2.3, R3.Pin_0
  N10: LED3.common_anode, R3.Pin_1
